// Logisim project Parcial2_S2_Maximiliano_Gonzalez.circ as structural Verilog: 18 circuits, main circuit ALU
module ALU (
  input  [1:0] OP,
  input  [6:0] A,
  input  [6:0] B,
  output [6:0] RES,
  output Z,
  output N,
  output C
);

  wire and_2_out, C_out, not_2_out, not_3_out, Overflow, SUB_ADD;
  wire [6:0] adder7bits_1_sum, andcirc_1_and_out, multiplexer_1_out, not_1_out, orcirc_1_or_out;

  assign not_1_out = ~B;  // NOT_Gate not_1, 7 bits wide
  Multiplexer #(.width(7)) multiplexer_1 (.in0(B), .in1(not_1_out), .out(multiplexer_1_out), .sel(SUB_ADD));
  not not_2 (not_2_out, OP[1]);
  not not_3 (not_3_out, OP[1]);
  and and_1 (SUB_ADD, OP[0], not_2_out);
  and and_2 (and_2_out, Overflow, not_3_out);
  LED V (.in(and_2_out));
  Adder7Bits adder7bits_1 (
    .A(A), .B(multiplexer_1_out), .ALU_Control(SUB_ADD), .Sum(adder7bits_1_sum), .C_out(C_out),
    .Overflow(Overflow));
  ANDCirc andcirc_1 (.A(A), .B(B), .AND_out(andcirc_1_and_out));
  ORCirc orcirc_1 (.A(A), .B(B), .OR_out(orcirc_1_or_out));
  LED led_1 (.in(Z));
  FlagZyN flagzyn_1 (.RES(RES), .Z(Z), .N(N));
  FlagC flagc_1 (.C_out(C_out), .OP1(OP[1]), .C(C));
  LED led_2 (.in(N));
  LED led_3 (.in(C));
  Multiplexer #(.select(2), .width(7)) multiplexer_2 (
    .in0(adder7bits_1_sum), .in1(adder7bits_1_sum), .in2(andcirc_1_and_out), .in3(orcirc_1_or_out),
    .out(RES), .sel(OP));
endmodule

module Adder0x01 (
  input  A,
  input  B,
  input  C_in,
  output S,
  output C_out
);

  wire and_1_out, and_2_out, xor_1_out;

  xor xor_1 (xor_1_out, A, B);
  xor xor_2 (S, xor_1_out, C_in);
  and and_1 (and_1_out, C_in, xor_1_out);
  and and_2 (and_2_out, A, B);
  or or_1 (C_out, and_1_out, and_2_out);
endmodule

module ANDCirc (
  input  [6:0] A,
  input  [6:0] B,
  output [6:0] AND_out
);

  assign AND_out = A & B;  // AND_Gate and_1, 7 bits wide
endmodule

module ORCirc (
  input  [6:0] A,
  input  [6:0] B,
  output [6:0] OR_out
);

  assign OR_out = A | B;  // OR_Gate or_1, 7 bits wide
endmodule

module Adder0x0111 (
  input  [6:0] A,
  input  [6:0] B,
  input  C_in,
  output [6:0] Sum,
  output Overflow,
  output C_out
);

  wire B0, B1, B2, B3, B4, B5, B6, C_0, C_1, C_2, C_3, C_4, C_5;

  xor xor_1 (Overflow, C_5, C_out);
  SubSelector subselector_1 (.B(B), .C_in(C_in), .B0(B0), .B1(B1), .B2(B2), .B3(B3), .B4(B4), .B5(B5), .B6(B6));
  Adder0x01 adder0x01_1 (.A(A[0]), .B(B0), .C_in(C_in), .S(Sum[0]), .C_out(C_0));
  Adder0x01 adder0x01_2 (.A(A[1]), .B(B1), .C_in(C_0), .S(Sum[1]), .C_out(C_1));
  Adder0x01 adder0x01_3 (.A(A[2]), .B(B2), .C_in(C_1), .S(Sum[2]), .C_out(C_2));
  Adder0x01 adder0x01_4 (.A(A[3]), .B(B3), .C_in(C_2), .S(Sum[3]), .C_out(C_3));
  Adder0x01 adder0x01_5 (.A(A[4]), .B(B4), .C_in(C_3), .S(Sum[4]), .C_out(C_4));
  Adder0x01 adder0x01_6 (.A(A[5]), .B(B5), .C_in(C_4), .S(Sum[5]), .C_out(C_5));
  Adder0x01 adder0x01_7 (.A(A[6]), .B(B6), .C_in(C_5), .S(Sum[6]), .C_out(C_out));

  // Other names for the same wires on the sheet: C_6 = C_out; S1 = Sum[0]; S2 = Sum[1]; S3 = Sum[2]; S4 = Sum[3];
  //   S5 = Sum[4]; S6 = Sum[5]; S7 = Sum[6]
endmodule

module SubSelector (
  input  [6:0] B,
  input  C_in,
  output B0,
  output B1,
  output B2,
  output B3,
  output B4,
  output B5,
  output B6
);

  xor xor_1 (B0, B[0], C_in);
  xor xor_2 (B1, B[1], C_in);
  xor xor_3 (B2, B[2], C_in);
  xor xor_4 (B3, B[3], C_in);
  xor xor_5 (B4, B[4], C_in);
  xor xor_6 (B5, B[5], C_in);
  xor xor_7 (B6, B[6], C_in);

  // Other names for the same wires on the sheet: B0_t = B[0]; B1_t = B[1]; B2_t = B[2]; B3_t = B[3]; B4_t = B[4];
  //   B5_t = B[5]; B6_t = B[6]
endmodule

module Adder7Bits (
  input  [6:0] A,
  input  [6:0] B,
  input  ALU_Control,
  output [6:0] Sum,
  output C_out,
  output Overflow
);

  wire C_0, C_1, C_2, C_3, C_4, C_5;

  xor xor_1 (Overflow, C_5, C_out);
  Adder0x01 adder0x01_1 (.A(A[0]), .B(B[0]), .C_in(ALU_Control), .S(Sum[0]), .C_out(C_0));
  Adder0x01 adder0x01_2 (.A(A[1]), .B(B[1]), .C_in(C_0), .S(Sum[1]), .C_out(C_1));
  Adder0x01 adder0x01_3 (.A(A[2]), .B(B[2]), .C_in(C_1), .S(Sum[2]), .C_out(C_2));
  Adder0x01 adder0x01_4 (.A(A[3]), .B(B[3]), .C_in(C_2), .S(Sum[3]), .C_out(C_3));
  Adder0x01 adder0x01_5 (.A(A[4]), .B(B[4]), .C_in(C_3), .S(Sum[4]), .C_out(C_4));
  Adder0x01 adder0x01_6 (.A(A[5]), .B(B[5]), .C_in(C_4), .S(Sum[5]), .C_out(C_5));
  Adder0x01 adder0x01_7 (.A(A[6]), .B(B[6]), .C_in(C_5), .S(Sum[6]), .C_out(C_out));

  // Other names for the same wires on the sheet: C_6 = C_out; S1 = Sum[0]; S2 = Sum[1]; S3 = Sum[2]; S4 = Sum[3];
  //   S5 = Sum[4]; S6 = Sum[5]; S7 = Sum[6]
endmodule

module ALU_SELECTOR (
  input  S1,
  input  S0,
  output SUM,
  output SUB,
  output AND_MODE,
  output OR_MODE
);

  wire not_1_out, not_2_out;

  not not_1 (not_1_out, S1);
  not not_2 (not_2_out, S0);
  and and_1 (SUM, not_1_out, not_2_out);
  and and_2 (SUB, not_1_out, S0);
  and and_3 (AND_MODE, S1, not_2_out);
  and and_4 (OR_MODE, S1, S0);
endmodule

module FlagZyN (
  input  [6:0] RES,
  output Z,
  output N
);

  wire or_1_out;

  or or_1 (or_1_out, RES[0], RES[1], RES[2], RES[3], RES[4], RES[5], RES[6]);
  not not_1 (Z, or_1_out);

  assign N = RES[6];
endmodule

module FlagC (
  input  C_out,
  input  OP1,
  output C
);

  Multiplexer multiplexer_1 (.in0(C_out), .in1(1'b0), .out(C), .sel(OP1));
endmodule

module ALUShiftersSoloA (
  input  [2:0] OP,
  input  [6:0] A,
  input  [6:0] B,
  output [6:0] RES,
  output C,
  output Z,
  output N
);

  wire and_2_out, C_out, not_1_out, not_2_out, not_4_out, not_5_out, Overflow, SHLACarry, SHRACarry, SUB_ADD;
  wire [6:0] adder7bits_1_sum, andcirc_1_and_out, multiplexer_1_out, not_3_out, orcirc_1_or_out, SHLA, SHRA;

  not not_1 (not_1_out, OP[1]);
  not not_2 (not_2_out, OP[2]);
  assign not_3_out = ~B;  // NOT_Gate not_3, 7 bits wide
  and and_1 (SUB_ADD, OP[0], not_1_out, not_2_out);
  Multiplexer #(.width(7)) multiplexer_1 (.in0(B), .in1(not_3_out), .out(multiplexer_1_out), .sel(SUB_ADD));
  not not_4 (not_4_out, OP[1]);
  not not_5 (not_5_out, OP[2]);
  and and_2 (and_2_out, Overflow, not_4_out, not_5_out);
  Adder7Bits adder7bits_1 (
    .A(A), .B(multiplexer_1_out), .ALU_Control(SUB_ADD), .Sum(adder7bits_1_sum), .C_out(C_out),
    .Overflow(Overflow));
  ANDCirc andcirc_1 (.A(A), .B(B), .AND_out(andcirc_1_and_out));
  ORCirc orcirc_1 (.A(A), .B(B), .OR_out(orcirc_1_or_out));
  ShiftLeftA shiftlefta_1 (.A(A), .SHLA(SHLA), .Carry(SHLACarry));
  ShiftRightA shiftrighta_1 (.A(A), .Carry(SHRACarry), .SHRA(SHRA));
  FlagCShifters flagcshifters_1 (
    .C_out(C_out), .OP1(OP[1]), .OP2(OP[2]), .SHLCarry(SHLACarry), .SHRCarry(SHRACarry), .OP0(OP[0]), .C(C));
  LED led_1 (.in(C));
  LED V (.in(and_2_out));
  LED led_2 (.in(Z));
  FlagZyN flagzyn_1 (.RES(RES), .Z(Z), .N(N));
  LED led_3 (.in(N));
  Multiplexer #(.select(3), .width(7)) multiplexer_2 (
    .in0(adder7bits_1_sum), .in1(adder7bits_1_sum), .in2(andcirc_1_and_out), .in3(orcirc_1_or_out),
    .in4(SHLA), .in5(SHRA), .out(RES), .sel(OP));  // open: in6, in7
endmodule

module ShiftLeft (
  input  A0,
  input  A1,
  input  A2,
  input  A3,
  input  Shift,
  input  A4,
  input  A5,
  input  A6,
  output [6:0] SHL
);

  Multiplexer #(.width(7)) multiplexer_1 (
    .in0({A6, A5, A4, A3, A2, A1, A0}), .in1({A5, A4, A3, A2, A1, A0, 1'b0}), .out(SHL), .sel(Shift));
endmodule

module ShiftRight (
  input  A0,
  input  A1,
  input  A2,
  input  A3,
  input  A4,
  input  Shift,
  input  A5,
  input  A6,
  output [6:0] SHR
);

  Multiplexer #(.width(7)) multiplexer_1 (
    .in0({A6, A5, A4, A3, A2, A1, A0}), .in1({1'b0, A6, A5, A4, A3, A2, A1}), .out(SHR), .sel(Shift));
endmodule

module ShiftLeftA (
  input  [6:0] A,
  output [6:0] SHLA,
  output Carry
);


  assign Carry = A[6];
  assign SHLA = {A[5:0], 1'b0};
endmodule

module ShiftRightA (
  input  [6:0] A,
  output Carry,
  output [6:0] SHRA
);


  assign Carry = A[0];
  assign SHRA = {1'b0, A[6:1]};
endmodule

module FlagCShifters (
  input  C_out,
  input  OP1,
  input  OP2,
  input  SHLCarry,
  input  SHRCarry,
  input  OP0,
  output C
);

  wire multiplexer_1_out, multiplexer_2_out;

  Multiplexer multiplexer_1 (.in0(C_out), .in1(1'b0), .out(multiplexer_1_out), .sel(OP1));
  Multiplexer multiplexer_2 (.in0(SHLCarry), .in1(SHRCarry), .out(multiplexer_2_out), .sel(OP0));
  Multiplexer multiplexer_3 (.in0(multiplexer_1_out), .in1(multiplexer_2_out), .out(C), .sel(OP2));
endmodule

module ALUShifterResult (
  input  [1:0] OP,
  input  [2:0] OP_2,
  input  [6:0] A,
  input  [6:0] B,
  output [6:0] BASE,
  output [6:0] RESULT,
  output C,
  output V,
  output Z,
  output N
);

  wire C_out, not_1_out, not_2_out, not_4_out, not_5_out, Overflow, SHLACarry, SHRACarry, SUB_ADD;
  wire [6:0] adder7bits_1_sum, andcirc_1_and_out, multiplexer_1_out, not_3_out, orcirc_1_or_out, SHLA, SHRA;

  not not_1 (not_1_out, OP_2[1]);
  not not_2 (not_2_out, OP_2[2]);
  and and_1 (SUB_ADD, OP_2[0], not_1_out, not_2_out);
  assign not_3_out = ~B;  // NOT_Gate not_3, 7 bits wide
  Multiplexer #(.width(7)) multiplexer_1 (.in0(B), .in1(not_3_out), .out(multiplexer_1_out), .sel(SUB_ADD));
  not not_4 (not_4_out, OP_2[1]);
  not not_5 (not_5_out, OP_2[2]);
  Adder7Bits adder7bits_1 (
    .A(A), .B(multiplexer_1_out), .ALU_Control(SUB_ADD), .Sum(adder7bits_1_sum), .C_out(C_out),
    .Overflow(Overflow));
  ANDCirc andcirc_1 (.A(A), .B(B), .AND_out(andcirc_1_and_out));
  ORCirc orcirc_1 (.A(A), .B(B), .OR_out(orcirc_1_or_out));
  ShiftLeftA shiftlefta_1 (.A(BASE), .SHLA(SHLA), .Carry(SHLACarry));
  ShiftRightA shiftrighta_1 (.A(BASE), .Carry(SHRACarry), .SHRA(SHRA));
  FlagCShifters flagcshifters_1 (
    .C_out(C_out), .OP1(OP_2[1]), .OP2(OP_2[2]), .SHLCarry(SHLACarry), .SHRCarry(SHRACarry), .OP0(OP_2[0]),
    .C(C));
  FlagZyN flagzyn_1 (.RES(RESULT), .Z(Z), .N(N));
  and and_2 (V, Overflow, not_4_out, not_5_out);
  Multiplexer #(.select(2), .width(7)) multiplexer_2 (
    .in0(adder7bits_1_sum), .in1(adder7bits_1_sum), .in2(andcirc_1_and_out), .in3(orcirc_1_or_out),
    .out(BASE), .sel(OP));
  LED LEDc (.in(C));
  LED LEDv (.in(V));
  LED LEDz (.in(Z));
  LED LEDn (.in(N));
  Multiplexer #(.select(3), .width(7)) multiplexer_3 (
    .in0(BASE), .in1(BASE), .in2(BASE), .in3(BASE), .in4(SHLA), .in5(SHRA), .out(RESULT), .sel(OP_2));  // open: in6, in7
  LedBar #(.matrixcols(7)) ledbar_1 (
    .led0(BASE[6]), .led1(BASE[5]), .led2(BASE[4]), .led3(BASE[3]), .led4(BASE[2]), .led5(BASE[1]),
    .led6(BASE[0]));
  LedBar #(.matrixcols(7)) ledbar_2 (
    .led0(RESULT[6]), .led1(RESULT[5]), .led2(RESULT[4]), .led3(RESULT[3]), .led4(RESULT[2]),
    .led5(RESULT[1]), .led6(RESULT[0]));

  // Other names for the same wires on the sheet: OP0_2 = OP_2[0]; OP1_2 = OP_2[1]; OP2_2 = OP_2[2]
endmodule

module ALUSHFINAL (
  input  [1:0] OP,
  input  [2:0] OP_2,
  input  [6:0] A,
  input  [6:0] B
);

  wire alushifterresult_1_c, alushifterresult_1_n, alushifterresult_1_v, alushifterresult_1_z;
  wire [6:0] alushifterresult_1_base, alushifterresult_1_result;

  ALUShifterResult alushifterresult_1 (
    .OP(OP), .OP_2(OP_2), .A(A), .B(B), .BASE(alushifterresult_1_base), .RESULT(alushifterresult_1_result),
    .C(alushifterresult_1_c), .V(alushifterresult_1_v), .Z(alushifterresult_1_z), .N(alushifterresult_1_n));
  LED C (.in(alushifterresult_1_c));
  LED V (.in(alushifterresult_1_v));
  LED Z (.in(alushifterresult_1_z));
  LED N (.in(alushifterresult_1_n));
  LedBar #(.matrixcols(7)) RESULT (
    .led0(alushifterresult_1_result[6]), .led1(alushifterresult_1_result[5]),
    .led2(alushifterresult_1_result[4]), .led3(alushifterresult_1_result[3]),
    .led4(alushifterresult_1_result[2]), .led5(alushifterresult_1_result[1]),
    .led6(alushifterresult_1_result[0]));
  LedBar #(.matrixcols(7)) BASE (
    .led0(alushifterresult_1_base[6]), .led1(alushifterresult_1_base[5]), .led2(alushifterresult_1_base[4]),
    .led3(alushifterresult_1_base[3]), .led4(alushifterresult_1_base[2]), .led5(alushifterresult_1_base[1]),
    .led6(alushifterresult_1_base[0]));
endmodule
